# Fritzing sketch electronics (saved by Fritzing 0.9.10b)
perfboards: 1

parts:
  U1 = ESP32S-HiLetgo [part_number=ESP32S-HiLetgo]
  YF-S201_Flow_Meter1 = YF-S201 Water Flow Meter
  Nokia_5110_LCD_Module1 = Nokia 5110 LCD
  X1 = USB Connectors [package=usb-minib-nostop]
  R1 = Temperature Sensor (Thermistor) [thermistor_type=NTC package=THT]
  R2 = Resistor [tolerance=±5% resistance=220 package="0805 [SMD]"]

nets:
  N1: U1.3.3, Nokia_5110_LCD_Module1.VCC, Nokia_5110_LCD_Module1.VCC_(out), R1.pin_0
  N2: U1.GPIO32, R1.pin_1, R2.Pin_1
  N3: U1.GPIO27, Nokia_5110_LCD_Module1.LED, Nokia_5110_LCD_Module1.LED_(out)
  N4: U1.GPIO14, Nokia_5110_LCD_Module1.RST, Nokia_5110_LCD_Module1.RST_(out)
  VIN: U1.VIN, YF-S201_Flow_Meter1.VCC, X1.VBUS
  N5: U1.GPIO5, Nokia_5110_LCD_Module1.SCE, Nokia_5110_LCD_Module1.SCE_(out)
  N6: U1.GPIO18, Nokia_5110_LCD_Module1.SCLK, Nokia_5110_LCD_Module1.SCLK_(out)
  N7: U1.GPIO19, Nokia_5110_LCD_Module1.D/C, Nokia_5110_LCD_Module1.D/C_(out)
  GND: U1.GND, YF-S201_Flow_Meter1.GND, Nokia_5110_LCD_Module1.GND, Nokia_5110_LCD_Module1.GND_(out), X1.GND, R2.Pin_0
  N8: U1.GPIO21, YF-S201_Flow_Meter1.SIG
  N9: U1.GPIO23, Nokia_5110_LCD_Module1.DN(MOSI), Nokia_5110_LCD_Module1.DN(MODI)_(out)

custom parts:
  ESP32S-HiLetgo: HiLetgo ESP-WROOM-32 ESP32 ESP-32S Development Board 2.4GHz Dual-Mode WiFi + Bluetooth Dual Cores Microcontroller The ESP32 integrated with Antenna switches, RF Balun, power amplifiers, low-noise amplifiers, filters, and management modules, and the entire solution occupies the least area of PCB. 2.4 GHz Wi-Fi plus Bluetooth dual-mode chip, with TSMC Ultra-low power consumption 40nm technology,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
  YF-S201 Water Flow Meter: The YF-S201 Flow Meter. The input voltage is 5V to 24V (DC).
  Nokia 5110 LCD: Nokia 5110 Graphic 84*48 LCD module such as the Sparkfun LCD-10168 or the clones from Ebay. There is example code for the Arduino available from the Sparkfun site in https://learn.sparkfun.com/tutorials/graphic-lcd-hookup-guide This is a 3.3V device, if you are running it from a 5V micro you need a 5V tolorant level translator such as the 74ahc367 to protect the signal imputs. Rafa G. did a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
